# Fritzing sketch Arduino实验十五：温湿度传感器实验 (saved by Fritzing 0.8.7b)
breadboards: 1

parts:
  元件1 = Arduino Uno (Rev3)
  U1 = DHT11

nets:
  N1: 元件1.D2, U1.IO
  5V: 元件1.5V, U1.VCC
  GND: 元件1.GND, U1.GND
