# Fritzing sketch Arduino实验十八：步进电机实验 (saved by Fritzing 0.8.7b)

parts:
  元件1 = Arduino Uno (Rev3)
  U1 = 步进电机
  U2 = 步进电机驱动

nets:
  N1: 元件1.D2, U2.BJ1
  N2: 元件1.D3_PWM, U2.BJ2
  N3: 元件1.D4, U2.BJ3
  N4: 元件1.D5_PWM, U2.BJ4
  5V: 元件1.5V, U2.VCC
  GND: 元件1.GND, U2.GND
  N5: U1.VCC, U2.VOUT1
  N6: U1.A, U2.A
  N7: U1.B, U2.B
  N8: U1.C, U2.C
  N9: U1.D, U2.D
